# Fritzing sketch BreadboardCircuit (saved by Fritzing 0.9.3b)
breadboards: 1

parts:
  KY-1 = Keyes Relay [package=THT]
  JP1 = Header 2 [package=screwterminal-3.5mm-2_lock]
  Part1 = Arduino Uno (Rev3)
  KY-2 = Keyes Relay [package=THT]
  LED1 = LEDs [package=led10mm]
  LED2 = LEDs [package=led10mm]
  JP2 = Header 2 [package=screwterminal-3.5mm-2_lock]
  IR1 = TSOP312.., 314.. [package=THT]
  LED3 = LED - 3mm [color="Red (633nm)" package="3 mm [THT]"]
  LED4 = LED - 3mm [color="Red (633nm)" package="3 mm [THT]"]
  R1 = Resistor [tolerance=±5% resistance=220 package="0603 [SMD]"]
  R2 = Resistor [tolerance=±5% resistance=220 package="0603 [SMD]"]

nets:
  N1: KY-1.signal, Part1.D6_PWM
  N2: KY-1.C, JP2.1
  N3: KY-1.NO, LED2.C
  N4: JP1.1, KY-2.C
  N5: JP1.2, LED1.A
  N6: Part1.D11_PWM/MOSI, R1.Pin_1
  N7: Part1.D12/MISO, R2.Pin_1
  N8: Part1.D5_PWM, IR1.Data
  N9: Part1.D7, KY-2.signal
  N10: Part1.5V, KY-2.power, IR1.Vs
  GND: Part1.GND, KY-2.ground, IR1.GND
  N11: KY-2.NO, LED1.C
  N12: LED2.A, JP2.2
  N13: LED3.cathode, LED4.cathode
  N14: LED3.anode, R2.Pin_0
  N15: LED4.anode, R1.Pin_0

custom parts:
  Keyes Relay: The Keyes 5V relay module is suitable for SCM development, home appliance control. It uses a 5V~12V TIL control signal which can control DC / AC signal.
  LEDs: LEDs Standard schematic elements and footprints for 5mm, 3mm, 1206, and 0603 sized LEDs. 5mm - Spark Fun Electronics SKU : COM-00529 (and others)
